// Logisim project 7-bit simulation.circ as structural Verilog: 1 circuit, main circuit main
module main (
  input  [2:0] Colour_selection,
  input  En,
  input  [2:0] Select_bits,
  input  [3:0] Select,
  output [2:0] _1,
  output A,
  output [2:0] _2,
  output B,
  output [2:0] _3,
  output C,
  output [2:0] _4,
  output D,
  output [2:0] _5,
  output E,
  output [2:0] _6,
  output F,
  output [2:0] _7,
  output G,
  output [2:0] _8,
  output DP,
  output [2:0] _9
);

  Demultiplexer #(.select(3), .enable("false")) demultiplexer_1 (
    .out0(A), .out1(B), .out2(C), .out3(D), .out4(E), .out5(F), .out6(G), .out7(DP), .in(En),
    .sel(Select_bits));
  Demultiplexer #(.select(4), .width(3), .enable("false")) demultiplexer_2 (
    .out0(_1), .out1(_2), .out2(_3), .out3(_4), .out4(_5), .out5(_6), .out6(_7), .out7(_8), .out8(_9),
    .in(Colour_selection), .sel(Select));  // open: out9, out10, out11, out12, out13, out14, out15
endmodule
